# Fritzing sketch RC_Car (saved by Fritzing 1.0.1rc)
breadboards: 1

parts:
  Raspberry_Pi_1 = Raspberry Pi 3 [part_number=RPI-3-V1.2]
  S5 = Toggle Switch [package=THT]
  VCC2 = Battery
  L298N1 = L298N DC motor driver
  M6 = DC Motor [voltage_(max)=6V voltage_(min)=3V]
  L298N2 = L298N DC motor driver
  J1 = Basic Servo
  M7 = DC Motor [voltage_(max)=6V voltage_(min)=3V]
  M8 = DC Motor [voltage_(max)=6V voltage_(min)=3V]
  Arduino_Nano_3 = Arduino Nano (Rev3.0) (ICSP)
  DHT1 = Humidity and Temperature Sensor DHT11
  LED1 = RGB LED (com. cathode, rbg) [package="5 mm [THT]"]
  LED2 = RGB LED (com. cathode, rbg) [package="5 mm [THT]"]
  LED3 = RGB LED (com. cathode, rbg) [package="5 mm [THT]"]
  VCC1 = Battery
  USBTTL1 = USB A Plug
  USBTTL2 = Micro USB B Plug
  R1 = Resistor [tolerance=±5% resistance=102 package="2512 [SMD]"]

nets:
  N1: Raspberry_Pi_1.GPIO2, S5.L1
  N2: Raspberry_Pi_1.GPIO3, DHT1.Data-signal, R1.Pin_1
  N3: Raspberry_Pi_1.GIPO27, LED2.red_anode
  N4: Raspberry_Pi_1.GIPO22, LED2.blue_anode
  N5: Raspberry_Pi_1.GIPO10, LED3.red_anode
  N6: Raspberry_Pi_1.GIPO9, LED3.blue_anode
  N7: Raspberry_Pi_1.GIPO11, LED3.green_anode
  N8: Raspberry_Pi_1.GIPO24, LED2.green_anode
  N9: Raspberry_Pi_1.GIPO18, LED1.green_anode
  N10: Raspberry_Pi_1.GIPO15, LED1.blue_anode
  N11: Raspberry_Pi_1.GIPO14, LED1.red_anode
  N12: S5.COM, VCC2.+, DHT1.Vcc, LED1.common_cathode, LED2.common_cathode, LED3.common_cathode, R1.Pin_0
  N13: S5.L2, VCC2.-, DHT1.GND_2
  N14: L298N1.OUT1, M7.pin_2
  N15: L298N1.OUT2, M7.pin_1
  N16: L298N1.OUT3, M8.pin_2
  N17: L298N1.OUT4, M8.pin_1
  12V: L298N1.12V, L298N2.12V, J1.vcc, VCC1.+
  GND: L298N1.GND, L298N2.GND, J1.gnd, VCC1.-
  N18: L298N1.5V#9, L298N1.ENA
  N19: L298N1.5V#10, L298N1.ENB
  N20: L298N1.IN1, Arduino_Nano_3.D10, Arduino_Nano_3.D11/MOSI, Arduino_Nano_3.D12/MISO
  N21: L298N1.IN2, Arduino_Nano_3.D9
  N22: L298N1.IN3, Arduino_Nano_3.D8
  N23: L298N1.IN4, Arduino_Nano_3.D7
  N24: M6.pin_1, L298N2.OUT2
  N25: M6.pin_2, L298N2.OUT1
  N26: L298N2.5V#9, L298N2.ENA
  N27: L298N2.5V#10, L298N2.ENB
  N28: L298N2.IN1, Arduino_Nano_3.D6
  N29: L298N2.IN2, Arduino_Nano_3.D5
  N30: J1.pulse, Arduino_Nano_3.D3
  N31: USBTTL1.usb, USBTTL2.usb

notes:
  6 Pilas x 1.2V
  PowerBank 5V
  Controlador Motor Rodes
  Right Motor
  Left Motor
  Nilon Motor
  Distribució eneregia powerbank
  Distribució eneregia motors
  Controlador Motor Nilon
  IO Arduino Nano
  D10: Left Wheel In 1
  D9: Left Wheel In 2
  D8: Right Wheel In 1
  D7: Right Wheel In 2
  D6: Nilon DC In 1
  D5: Nilon DC In 2
  D3: Servo In
  IO Raspberry Pi:
  GPIO2: Switch In data
  GPIO3: DHT1 In data
  GPIO14: R Out LED1
  GPIO15: G Out LED1
  GPIO15: B Out LED1
  GPIO27: R Out LED2
  GPIO22: G Out LED2
  GPIO24: B Out LED2
  GPIO10: R Out LED3
  GPIO9: G Out LED3
  GPIO11: B Out LED3
  L298N Input sheet
  IN1: Fordward
  IN2: Backward

custom parts:
  L298N DC motor driver: 2x DC motor driver with 78M05 positive voltage regulator (7..35 V) L298N: max 46 V, 2 A Set 5 V Enable jumper to enable 5 V regultor (needed for the L298N) and +5 V output at screw terminal or supply external +5 V at screw terminal Set ENA and/or ENB to +5 V to enable motor permanently or supply ENA and/or ENB with PWM signal IN1 and IN2 set rotation directory for motor A (OUT1/OUT2) IN2 and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
  Humidity and Temperature Sensor DHT11: Digital relative humidity & temperature sensor DHT11
