# Fritzing sketch GMR_AI (saved by Fritzing 1.0.1rc)
breadboards: 1

parts:
  VCC2 = Battery  # not connected
  L298N1 = L298N DC motor driver
  M6 = DC Motor [voltage_(max)=6V voltage_(min)=3V]
  L298N2 = L298N DC motor driver
  VCC1 = Battery
  J2 = Basic Servo
  Part2 = 16-Channel 12-bit PWM Servo Driver - I2C [part_number=815]
  Part3 = 10-DOF IMU L3GD20H + LSM303 + BMP180 [part_number=1604]
  DC_Mot_Enc1 = DC Motor with two-phase hall-encoder [part_number=VT-E-G25A-06-177E]
  DC_Mot_Enc2 = DC Motor with two-phase hall-encoder [part_number=VT-E-G25A-06-177E]
  Jetson_Nano1 = jetsonnano
  USBTTL1 = Micro USB B Plug  # not connected

nets:
  N1: L298N1.OUT1, DC_Mot_Enc2.pin6
  N2: L298N1.OUT2, DC_Mot_Enc2.pin1
  N3: L298N1.OUT3, DC_Mot_Enc1.pin6
  N4: L298N1.OUT4, DC_Mot_Enc1.pin1
  12V: L298N1.12V, L298N2.12V, L298N2.GND, VCC1.+
  N5: L298N1.GND, VCC1.-
  N6: L298N1.5V#9, L298N1.ENA
  N7: L298N1.5V#10, L298N1.ENB
  N8: L298N1.IN1, Jetson_Nano1.connector1
  N9: L298N1.IN2, Jetson_Nano1.connector2
  N10: L298N1.IN3, Jetson_Nano1.connector3
  N11: L298N1.IN4, Jetson_Nano1.connector35
  N12: M6.pin_1, L298N2.OUT2
  N13: M6.pin_2, L298N2.OUT1
  N14: L298N2.5V#9, L298N2.ENA
  N15: L298N2.5V#10, L298N2.ENB, L298N2.IN4
  N16: L298N2.IN1, Jetson_Nano1.connector32
  N17: L298N2.IN2, Jetson_Nano1.connector31
  GND: J2.gnd, Part2.GND, Part3.GND, DC_Mot_Enc1.pin2, DC_Mot_Enc1.pin5, DC_Mot_Enc2.pin2, Jetson_Nano1.connector23
  N18: J2.vcc, Part2.5.0V, Jetson_Nano1.connector19
  N19: J2.pulse, Part2.PWM15
  N20: Part2.VCC, Jetson_Nano1.connector20
  N21: Part3.VIN, DC_Mot_Enc2.pin5, Jetson_Nano1.connector39
  N22: Part3.SCL, Jetson_Nano1.connector14
  N23: Part3.SDA, Jetson_Nano1.connector15
  N24: DC_Mot_Enc1.pin3, Jetson_Nano1.connector22
  N25: DC_Mot_Enc1.pin4, Jetson_Nano1.connector21
  N26: DC_Mot_Enc2.pin3, Jetson_Nano1.connector29
  N27: DC_Mot_Enc2.pin4, Jetson_Nano1.connector28

notes:
  6 Pilas x 1.2V
  Bateria 5V
  Controlador Motor Rodes
  Right Motor
  Left Motor
  Nilon Motor
  Controlador Motor Nilon
  IO Nvidia Jetson Nano:
  GPIO2: Left Motor In 1
  GPIO3: Left Motor In 2
  GPIO4: Right Motor In 1
  GPIO15: Right Motor In 1
  GPIO23: Nilon Motor In 1
  GPIO24: Nilon Motor In 2
  GPIO25: Left Motor Encoder Phase A In
  GPIO28: Left Motor Encoder Phase B In
  GPIO16: Right Motor Encoder Phase A In
  GPIO20: Right Motor Encoder Phase B In
  GPIO 5: IMU SCL In
  GPIO 6: IMU SDA In
  Motor+encoder binding:
  Red - Motor +
  Black - Encoder +
  Yellow - Encoder Phase A
  Green - Encoder Phase B
  Blue - Encoder -
  Gray - Motor -

custom parts:
  L298N DC motor driver: 2x DC motor driver with 78M05 positive voltage regulator (7..35 V) L298N: max 46 V, 2 A Set 5 V Enable jumper to enable 5 V regultor (needed for the L298N) and +5 V output at screw terminal or supply external +5 V at screw terminal Set ENA and/or ENB to +5 V to enable motor permanently or supply ENA and/or ENB with PWM signal IN1 and IN2 set rotation directory for motor A (OUT1/OUT2) IN2 and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
  16-Channel 12-bit PWM Servo Driver - I2C: You want to make a cool robot, maybe a hexapod walker, or maybe just a piece of art with a lot of moving parts. Or maybe you want to drive a lot of LEDs with precise PWM output. Using only two pins, control 16 free-running PWM outputs! You can even chain up 62 breakouts to control up to 992 PWM outputs.
  10-DOF IMU L3GD20H + LSM303 + BMP180: This inertial-measurement-unit combines 3 of the best quality sensors available on the market to give you 11 axes of data: 3 axes of accelerometer data, 3 axes gyroscopic, 3 axes magnetic (compass), barometric pressure/altitude and temperature. We tested many different 'combination' sensors and found these were the best value, with stable and reliable readings.
