# Fritzing sketch RC_Car (saved by Fritzing 0.9.6b)
breadboards: 1

parts:
  VCC2 = Battery  # not connected
  L298N1 = L298N DC motor driver
  M6 = DC Motor [voltage_(max)=6V voltage_(min)=3V]
  L298N2 = L298N DC motor driver
  VCC1 = Battery  # not connected
  BAT2 = BC9VPC [package=bc9vpc]  # not connected
  J2 = Basic Servo
  Part2 = 16-Channel 12-bit PWM Servo Driver - I2C [part_number=815]
  Jetson_Nano2 = jetsonnano
  U1 = IMU3000 [package=qfn-24]  # not connected
  Part3 = 10-DOF IMU L3GD20H + LSM303 + BMP180 [part_number=1604]  # not connected
  DC_Mot_Enc1 = DC Motor with two-phase hall-encoder [part_number=VT-E-G25A-06-177E]
  DC_Mot_Enc2 = DC Motor with two-phase hall-encoder [part_number=VT-E-G25A-06-177E]

nets:
  N1: L298N1.OUT1, DC_Mot_Enc2.pin2
  N2: L298N1.OUT2, DC_Mot_Enc2.pin1
  N3: L298N1.OUT3, DC_Mot_Enc1.pin2
  N4: L298N1.OUT4, DC_Mot_Enc1.pin1
  N5: L298N1.5V#9, L298N1.ENA
  N6: L298N1.5V#10, L298N1.ENB
  N7: L298N1.IN1, Jetson_Nano2.connector1
  N8: L298N1.IN2, Jetson_Nano2.connector2
  N9: L298N1.IN3, Jetson_Nano2.connector3
  N10: L298N1.IN4, Jetson_Nano2.connector35
  N11: M6.pin_1, L298N2.OUT2
  N12: M6.pin_2, L298N2.OUT1
  N13: L298N2.5V#9, L298N2.ENA
  N14: L298N2.5V#10, L298N2.ENB, L298N2.IN4
  N15: L298N2.IN1, Jetson_Nano2.connector32
  N16: L298N2.IN2, Jetson_Nano2.connector31
  GND: J2.gnd, Part2.GND
  N17: J2.pulse, Part2.PWM15
  N18: Part2.5.0V, Jetson_Nano2.connector19
  N19: Part2.VCC, Jetson_Nano2.connector20

notes:
  6 Pilas x 1.2V
  PowerBank 5V
  Controlador Motor Rodes
  Right Motor
  Left Motor
  Nilon Motor
  Controlador Motor Nilon
  IO Arduino Nano
  D10: Left Wheel In 1
  D9: Left Wheel In 2
  D8: Right Wheel In 1
  D7: Right Wheel In 2
  D6: Nilon DC In 1
  D5: Nilon DC In 2
  D3: Servo In
  IO Raspberry Pi:
  GPIO2: Switch In data
  GPIO3: DHT1 In data
  GPIO14: R Out LED1
  GPIO15: G Out LED1
  GPIO15: B Out LED1
  GPIO27: R Out LED2
  GPIO22: G Out LED2
  GPIO24: B Out LED2
  GPIO10: R Out LED3
  GPIO9: G Out LED3
  GPIO11: B Out LED3
  1 - Motor +
  2 - Encoder +
  3 - Encoder Phase A
  4 - Encoder Phase B
  5 - Encoder -
  6 - Motor -

custom parts:
  L298N DC motor driver: 2x DC motor driver with 78M05 positive voltage regulator (7..35 V) L298N: max 46 V, 2 A Set 5 V Enable jumper to enable 5 V regultor (needed for the L298N) and +5 V output at screw terminal or supply external +5 V at screw terminal Set ENA and/or ENB to +5 V to enable motor permanently or supply ENA and/or ENB with PWM signal IN1 and IN2 set rotation directory for motor A (OUT1/OUT2) IN2 and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
  16-Channel 12-bit PWM Servo Driver - I2C: You want to make a cool robot, maybe a hexapod walker, or maybe just a piece of art with a lot of moving parts. Or maybe you want to drive a lot of LEDs with precise PWM output. Using only two pins, control 16 free-running PWM outputs! You can even chain up 62 breakouts to control up to 992 PWM outputs.
  10-DOF IMU L3GD20H + LSM303 + BMP180: This inertial-measurement-unit combines 3 of the best quality sensors available on the market to give you 11 axes of data: 3 axes of accelerometer data, 3 axes gyroscopic, 3 axes magnetic (compass), barometric pressure/altitude and temperature. We tested many different 'combination' sensors and found these were the best value, with stable and reliable readings.
